// Digital circuit Questão 2.55.dig as structural Verilog
module \Questão_2_55  (
  input  m1,
  input  m2,
  input  m3,
  input  m4,
  input  m5,
  input  m6,
  input  m7,
  input  m8,
  input  m9,
  input  m0,
  output A
);

  wire and_1_out, and_2_out, and_3_out, and_4_out, and_5_out, and_6_out, and_7_out, and_8_out, and_9_out,
       and_10_out, and_11_out, or_1_out;

  and and_1 (and_1_out, ~m0, ~m1, ~m2, ~m3, ~m4, ~m5, ~m6, ~m7, ~m8, m9);  // And
  and and_2 (and_2_out, ~m0, ~m1, ~m2, ~m3, ~m4, ~m5, ~m6, ~m7, m8, ~m9);  // And
  and and_3 (and_3_out, ~m0, ~m1, ~m2, ~m3, ~m4, ~m5, ~m6, m7, ~m8, ~m9);  // And
  and and_4 (and_4_out, ~m0, ~m1, ~m2, ~m3, ~m4, ~m5, m6, ~m7, ~m8, ~m9);  // And
  and and_5 (and_5_out, ~m0, ~m1, ~m2, ~m3, ~m4, m5, ~m6, ~m7, ~m8, ~m9);  // And
  not not_1 (A, or_1_out);
  or or_1 (or_1_out, and_11_out, and_10_out, and_9_out, and_8_out, and_7_out, and_6_out, and_5_out, and_4_out, and_3_out, and_2_out, and_1_out);
  and and_6 (and_6_out, ~m0, ~m1, ~m2, ~m3, m4, ~m5, ~m6, ~m7, ~m8, ~m9);  // And
  and and_7 (and_7_out, ~m0, ~m1, ~m2, m3, ~m4, ~m5, ~m6, ~m7, ~m8, ~m9);  // And
  and and_8 (and_8_out, ~m0, ~m1, m2, ~m3, ~m4, ~m5, ~m6, ~m7, ~m8, ~m9);  // And
  and and_9 (and_9_out, ~m0, m1, ~m2, ~m3, ~m4, ~m5, ~m6, ~m7, ~m8, ~m9);  // And
  and and_10 (and_10_out, m0, ~m1, ~m2, ~m3, ~m4, ~m5, ~m6, ~m7, ~m8, ~m9);  // And
  and and_11 (and_11_out, ~m0, ~m1, ~m2, ~m3, ~m4, ~m5, ~m6, ~m7, ~m8, ~m9);  // And
endmodule
