// Digital circuit alternativa-a.dig as structural Verilog
module alternativa_a (
  input  clk,
  input  A,
  input  B,
  input  C,
  output S
);

  wire and_1_out, xor_1_out;

  and and_1 (and_1_out, A, B);
  xor xor_1 (xor_1_out, and_1_out, C);
  D_FF d_ff_1 (.D(xor_1_out), .C(clk), .Q(S));  // open: nQ
endmodule
