// Digital circuit alternativa-b.dig as structural Verilog
module alternativa_b (
  input  clk,
  input  A,
  input  B,
  input  C,
  input  D,
  input  E,
  input  F,
  input  G,
  input  H,
  input  clk_2,
  output S1,
  output S2
);

  wire nand_1_out, nand_2_out, xnor_1_out, xor_1_out, xor_2_out, xor_3_out;

  xor xor_1 (xor_1_out, A, B);
  nand nand_1 (nand_1_out, D, E);
  xor xor_2 (xor_2_out, xor_1_out, C);
  nand nand_2 (nand_2_out, nand_1_out, F);
  xor xor_3 (xor_3_out, nand_2_out, G);
  D_FF d_ff_1 (.D(xor_2_out), .C(clk), .Q(S1));  // open: nQ
  xnor xnor_1 (xnor_1_out, xor_3_out, H);
  D_FF d_ff_2 (.D(xnor_1_out), .C(clk_2), .Q(S2));  // open: nQ
endmodule
