// Digital circuit alternativa-c.dig as structural Verilog
module alternativa_c (
  input  A,
  input  B,
  input  clk,
  input  C,
  input  D,
  input  clk_2,
  output S_NAND,
  output S_XOR
);

  wire nand_1_out, xor_1_out;

  nand nand_1 (nand_1_out, A, B);
  xor xor_1 (xor_1_out, C, D);
  D_FF d_ff_1 (.D(nand_1_out), .C(clk), .nQ(S_NAND));  // open: Q
  D_FF d_ff_2 (.D(xor_1_out), .C(clk_2), .nQ(S_XOR));  // open: Q
endmodule
